// Logisim project lab2_part1.circ as structural Verilog
module mux2to1 (
  input  x,
  input  y,
  input  s,
  output m
);

  wire and_1_out, and_2_out, not_1_out;

  not not_1 (not_1_out, s);
  and and_1 (and_1_out, x, not_1_out);
  and and_2 (and_2_out, s, y);
  or or_1 (m, and_1_out, and_2_out);
endmodule

module mux4to1 (
  input  u,
  input  v,
  input  w,
  input  x,
  input  s0,
  input  s1,
  output m
);

  wire mux2to1_1_m, mux2to1_2_m;

  mux2to1 mux2to1_1 (.x(u), .y(v), .s(s0), .m(mux2to1_1_m));
  mux2to1 mux2to1_2 (.x(w), .y(x), .s(s0), .m(mux2to1_2_m));
  mux2to1 mux2to1_3 (.x(mux2to1_1_m), .y(mux2to1_2_m), .s(s1), .m(m));
endmodule
