// Logisim project lab2_part2.circ as structural Verilog: 9 circuits, main circuit main
module main (
  input  SW3,
  input  SW2,
  input  SW1,
  input  SW0
);

  wire hex_decoder_1_s0, hex_decoder_1_s1, hex_decoder_1_s2, hex_decoder_1_s3, hex_decoder_1_s4,
       hex_decoder_1_s5, hex_decoder_1_s6;

  HEX_DECODER hex_decoder_1 (
    .SW3(SW3), .SW2(SW2), .SW1(SW1), .SW0(SW0), .S0(hex_decoder_1_s0), .S1(hex_decoder_1_s1),
    .S2(hex_decoder_1_s2), .S3(hex_decoder_1_s3), .S4(hex_decoder_1_s4), .S5(hex_decoder_1_s5),
    .S6(hex_decoder_1_s6));
  _7_Segment_Display u_7_segment_display_1 (
    .g(hex_decoder_1_s6), .f(hex_decoder_1_s5), .a(hex_decoder_1_s0), .b(hex_decoder_1_s1),
    .e(hex_decoder_1_s4), .d(hex_decoder_1_s3), .c(hex_decoder_1_s2));  // open: dp
endmodule

module HEX0 (
  input  D3,
  input  D2,
  input  D1,
  input  D0,
  output S0
);

  wire and_1_out, and_2_out, and_3_out, and_4_out, and_5_out, and_6_out, and_7_out, and_8_out, not_1_out,
       not_2_out, not_3_out, not_4_out, or_1_out, or_2_out, or_3_out, or_4_out;

  not not_1 (not_1_out, D3);
  not not_2 (not_2_out, D2);
  not not_3 (not_3_out, D0);
  not not_4 (not_4_out, D1);
  and and_1 (and_1_out, not_1_out, D1);
  and and_2 (and_2_out, D2, D1);
  and and_3 (and_3_out, not_1_out, D2);
  and and_4 (and_4_out, not_2_out, not_3_out);
  and and_5 (and_5_out, D3, not_3_out);
  and and_6 (and_6_out, D3, not_2_out);
  and and_7 (and_7_out, and_3_out, D0);
  and and_8 (and_8_out, and_6_out, not_4_out);
  or or_1 (or_1_out, and_1_out, and_2_out);
  or or_2 (or_2_out, and_7_out, and_4_out);
  or or_3 (or_3_out, and_5_out, and_8_out);
  or or_4 (or_4_out, or_2_out, or_3_out);
  or or_5 (S0, or_1_out, or_4_out);
endmodule

module HEX1 (
  input  D3,
  input  D2,
  input  D1,
  input  D0,
  output S1
);

  wire and_1_out, and_2_out, and_3_out, and_4_out, and_5_out, and_6_out, and_7_out, and_8_out, not_1_out,
       not_2_out, not_3_out, not_4_out, or_1_out, or_2_out, or_3_out;

  not not_1 (not_1_out, D3);
  not not_2 (not_2_out, D2);
  not not_3 (not_3_out, D1);
  not not_4 (not_4_out, D0);
  and and_1 (and_1_out, not_1_out, not_2_out);
  and and_2 (and_2_out, not_2_out, not_4_out);
  and and_3 (and_3_out, not_1_out, not_3_out);
  and and_4 (and_4_out, not_1_out, D1);
  and and_5 (and_5_out, D3, not_3_out);
  and and_6 (and_6_out, and_3_out, not_4_out);
  and and_7 (and_7_out, and_4_out, D0);
  and and_8 (and_8_out, and_5_out, D0);
  or or_1 (or_1_out, and_1_out, and_2_out);
  or or_2 (or_2_out, and_6_out, and_7_out);
  or or_3 (or_3_out, or_1_out, or_2_out);
  or or_4 (S1, or_3_out, and_8_out);
endmodule

module HEX2 (
  input  D3,
  input  D2,
  input  D1,
  input  D0,
  output S2
);

  wire and_1_out, and_2_out, and_3_out, and_4_out, and_5_out, not_1_out, not_2_out, not_3_out, or_1_out,
       or_2_out, or_3_out;

  not not_1 (not_1_out, D3);
  not not_2 (not_2_out, D2);
  not not_3 (not_3_out, D1);
  and and_1 (and_1_out, not_1_out, not_3_out);
  and and_2 (and_2_out, not_1_out, D0);
  and and_3 (and_3_out, not_1_out, D2);
  and and_4 (and_4_out, D3, not_2_out);
  and and_5 (and_5_out, not_3_out, D0);
  or or_1 (or_1_out, and_1_out, and_2_out);
  or or_2 (or_2_out, and_3_out, and_4_out);
  or or_3 (or_3_out, or_1_out, or_2_out);
  or or_4 (S2, or_3_out, and_5_out);
endmodule

module HEX3 (
  input  D3,
  input  D2,
  input  D1,
  input  D0,
  output S3
);

  wire and_1_out, and_2_out, and_3_out, and_4_out, and_5_out, and_6_out, and_7_out, and_8_out, and_9_out,
       and_10_out, not_1_out, not_2_out, not_3_out, not_4_out, or_1_out, or_2_out, or_3_out;

  not not_1 (not_1_out, D3);
  not not_2 (not_2_out, D2);
  not not_3 (not_3_out, D1);
  not not_4 (not_4_out, D0);
  and and_1 (and_1_out, D3, not_3_out);
  and and_2 (and_2_out, D2, not_3_out);
  and and_3 (and_3_out, D2, D1);
  and and_4 (and_4_out, not_1_out, not_2_out);
  and and_5 (and_5_out, not_2_out, D1);
  and and_6 (and_6_out, and_1_out, not_4_out);
  and and_7 (and_7_out, and_2_out, D0);
  and and_8 (and_8_out, and_3_out, not_4_out);
  and and_9 (and_9_out, and_4_out, not_4_out);
  and and_10 (and_10_out, and_5_out, D0);
  or or_1 (or_1_out, and_6_out, and_7_out);
  or or_2 (or_2_out, and_8_out, and_9_out);
  or or_3 (or_3_out, or_2_out, and_10_out);
  or or_4 (S3, or_1_out, or_3_out);
endmodule

module HEX4 (
  input  D3,
  input  D2,
  input  D1,
  input  D0,
  output S4
);

  wire and_1_out, and_2_out, and_3_out, and_4_out, and_5_out, not_1_out, not_2_out, or_1_out, or_2_out,
       or_3_out;

  not not_1 (not_1_out, D2);
  not not_2 (not_2_out, D0);
  and and_1 (and_1_out, D3, D1);
  and and_2 (and_2_out, D3, not_2_out);
  and and_3 (and_3_out, D3, D2);
  and and_4 (and_4_out, D1, not_2_out);
  and and_5 (and_5_out, not_1_out, not_2_out);
  or or_1 (or_1_out, and_1_out, and_2_out);
  or or_2 (or_2_out, and_3_out, and_4_out);
  or or_3 (or_3_out, or_2_out, and_5_out);
  or or_4 (S4, or_1_out, or_3_out);
endmodule

module HEX5 (
  input  D3,
  input  D2,
  input  D1,
  input  D0,
  output S5
);

  wire and_1_out, and_2_out, and_3_out, and_4_out, and_5_out, and_6_out, and_7_out, not_1_out, not_2_out,
       not_3_out, not_4_out, or_1_out, or_2_out, or_3_out;

  not not_1 (not_1_out, D3);
  not not_2 (not_2_out, D2);
  not not_3 (not_3_out, D1);
  not not_4 (not_4_out, D0);
  and and_1 (and_1_out, D3, not_2_out);
  and and_2 (and_2_out, D3, D1);
  and and_3 (and_3_out, not_3_out, not_4_out);
  and and_4 (and_4_out, not_1_out, D2);
  and and_5 (and_5_out, not_1_out, D2);
  and and_6 (and_6_out, and_4_out, not_4_out);
  and and_7 (and_7_out, and_5_out, not_3_out);
  or or_1 (or_1_out, and_1_out, and_2_out);
  or or_2 (or_2_out, and_3_out, and_6_out);
  or or_3 (or_3_out, or_2_out, and_7_out);
  or or_4 (S5, or_1_out, or_3_out);
endmodule

module HEX6 (
  input  D3,
  input  D2,
  input  D1,
  input  D0,
  output S6
);

  wire and_1_out, and_2_out, and_3_out, and_4_out, and_5_out, and_6_out, and_7_out, not_1_out, not_2_out,
       not_3_out, not_4_out, or_1_out, or_2_out, or_3_out, or_4_out;

  not not_1 (not_1_out, D3);
  not not_2 (not_2_out, D2);
  not not_3 (not_3_out, D1);
  not not_4 (not_4_out, D0);
  and and_1 (and_1_out, D3, not_2_out);
  and and_2 (and_2_out, D3, D0);
  and and_3 (and_3_out, D3, D1);
  and and_4 (and_4_out, D1, not_4_out);
  and and_5 (and_5_out, not_2_out, D1);
  and and_6 (and_6_out, not_1_out, D2);
  and and_7 (and_7_out, not_3_out, and_6_out);
  or or_1 (or_1_out, and_1_out, and_2_out);
  or or_2 (or_2_out, and_3_out, and_4_out);
  or or_3 (or_3_out, and_5_out, and_7_out);
  or or_4 (or_4_out, or_2_out, or_3_out);
  or or_5 (S6, or_1_out, or_4_out);
endmodule

module HEX_DECODER (
  input  SW3,
  input  SW2,
  input  SW1,
  input  SW0,
  output S0,
  output S1,
  output S2,
  output S3,
  output S4,
  output S5,
  output S6
);

  HEX0 hex0_1 (.D3(SW3), .D2(SW2), .D1(SW1), .D0(SW0), .S0(S0));
  HEX1 hex1_1 (.D3(SW3), .D2(SW2), .D1(SW1), .D0(SW0), .S1(S1));
  HEX2 hex2_1 (.D3(SW3), .D2(SW2), .D1(SW1), .D0(SW0), .S2(S2));
  HEX3 hex3_1 (.D3(SW3), .D2(SW2), .D1(SW1), .D0(SW0), .S3(S3));
  HEX4 hex4_1 (.D3(SW3), .D2(SW2), .D1(SW1), .D0(SW0), .S4(S4));
  HEX5 hex5_1 (.D3(SW3), .D2(SW2), .D1(SW1), .D0(SW0), .S5(S5));
  HEX6 hex6_1 (.D3(SW3), .D2(SW2), .D1(SW1), .D0(SW0), .S6(S6));
endmodule
