// Logisim project lab1_part2.circ as structural Verilog: 1 circuit, main circuit main
module main (
  input  a,
  input  b,
  input  c,
  output out_4
);

  wire n7404_1_pin2, n7404_1_pin3, n7404_1_pin4, n7404_1_pin7, n7404_1_pin14, n7408_1_pin3;

  _7404 #(.ShowInternalStructure("true"), .VccGndPorts("true")) u_7404_1 (
    .pin1(b), .pin2(n7404_1_pin2), .pin3(n7404_1_pin3), .pin4(n7404_1_pin4), .pin7(n7404_1_pin7),
    .pin14(n7404_1_pin14));  // open: pin5, pin6, pin13, pin12, pin11, pin10, pin9, pin8
  _7408 #(.ShowInternalStructure("true"), .VccGndPorts("true")) u_7408_1 (
    .pin1(c), .pin2(n7404_1_pin2), .pin3(n7408_1_pin3), .pin7(n7404_1_pin7), .pin14(n7404_1_pin14));  // open: pin4, pin5, pin6, pin13, pin12, pin11, pin10, pin9, pin8
  _7432 #(.ShowInternalStructure("true"), .VccGndPorts("true")) u_7432_1 (
    .pin1(a), .pin2(b), .pin3(n7404_1_pin3), .pin4(n7404_1_pin4), .pin5(n7408_1_pin3), .pin6(out_4),
    .pin7(n7404_1_pin7), .pin14(n7404_1_pin14));  // open: pin13, pin12, pin11, pin10, pin9, pin8
  // also tied to GND on the sheet: n7404_1_pin7
  // also tied to VCC on the sheet: n7404_1_pin14
endmodule
