// Logisim project lab1_part2_reduced.circ as structural Verilog: 1 circuit, main circuit main
module main (
  input  a,
  input  c,
  output f
);

  wire n7404_1_pin2, n7404_1_pin7, n7404_1_pin14;

  _7404 #(.ShowInternalStructure("true"), .VccGndPorts("true")) u_7404_1 (
    .pin1(a), .pin2(n7404_1_pin2), .pin7(n7404_1_pin7), .pin14(n7404_1_pin14));  // open: pin3, pin4, pin5, pin6, pin13, pin12, pin11, pin10, pin9, pin8
  _7432 #(.ShowInternalStructure("true"), .VccGndPorts("true")) u_7432_1 (
    .pin1(n7404_1_pin2), .pin2(c), .pin3(f), .pin7(n7404_1_pin7), .pin14(n7404_1_pin14));  // open: pin4, pin5, pin6, pin13, pin12, pin11, pin10, pin9, pin8
  // also tied to GND on the sheet: n7404_1_pin7
  // also tied to VCC on the sheet: n7404_1_pin14
endmodule
